// Logisim project Assignment 2.circ as structural Verilog: 9 circuits, main circuit main
module main (
  input  in_1,
  input  in_2,
  output out_3,
  output out_4
);

  HalfAdder halfadder_1 (.input_X(in_1), .input_Y(in_2), .Sum(out_3), .Carry(out_4));
endmodule

module HalfAdder (
  input  input_X,
  input  input_Y,
  output Sum,
  output Carry
);

  xor xor_1 (Sum, input_X, input_Y);
  and and_1 (Carry, input_X, input_Y);
endmodule

module FullAdder (
  input  input_X,
  input  input_Y,
  input  Cin,
  output Sum,
  output out_5
);

  wire halfadder_1_carry, halfadder_1_sum, halfadder_2_carry;

  HalfAdder halfadder_1 (.input_X(input_X), .input_Y(input_Y), .Sum(halfadder_1_sum), .Carry(halfadder_1_carry));
  HalfAdder halfadder_2 (.input_X(halfadder_1_sum), .input_Y(Cin), .Sum(Sum), .Carry(halfadder_2_carry));
  or or_1 (out_5, halfadder_2_carry, halfadder_1_carry);
endmodule

module Adder_8bit (
  input  Cin,
  input  X0,
  input  Y0,
  input  X1,
  input  Y1,
  input  X2,
  input  Y2,
  input  X3,
  input  Y3,
  input  X4,
  input  Y4,
  input  X5,
  input  Y5,
  input  X6,
  input  Y6,
  input  X7,
  input  Y7,
  output S0,
  output S1,
  output S2,
  output S3,
  output S4,
  output S5,
  output S6,
  output S7
);

  wire halfadder_1_carry, halfadder_1_sum, halfadder_2_carry, halfadder_2_sum, halfadder_3_carry,
       halfadder_3_sum, halfadder_4_carry, halfadder_4_sum, halfadder_5_carry, halfadder_5_sum,
       halfadder_6_carry, halfadder_6_sum, halfadder_7_carry, halfadder_7_sum, halfadder_8_carry,
       halfadder_8_sum, halfadder_9_carry, halfadder_10_carry, halfadder_11_carry, halfadder_12_carry,
       halfadder_13_carry, halfadder_14_carry, halfadder_15_carry, halfadder_16_carry, or_1_out, or_2_out,
       or_3_out, or_4_out, or_5_out, or_6_out, or_7_out, or_8_out;

  HalfAdder halfadder_1 (.input_X(X0), .input_Y(Y0), .Sum(halfadder_1_sum), .Carry(halfadder_1_carry));
  HalfAdder halfadder_2 (.input_X(X1), .input_Y(Y1), .Sum(halfadder_2_sum), .Carry(halfadder_2_carry));
  HalfAdder halfadder_3 (.input_X(X2), .input_Y(Y2), .Sum(halfadder_3_sum), .Carry(halfadder_3_carry));
  HalfAdder halfadder_4 (.input_X(X3), .input_Y(Y3), .Sum(halfadder_4_sum), .Carry(halfadder_4_carry));
  HalfAdder halfadder_5 (.input_X(X4), .input_Y(Y4), .Sum(halfadder_5_sum), .Carry(halfadder_5_carry));
  HalfAdder halfadder_6 (.input_X(X5), .input_Y(Y5), .Sum(halfadder_6_sum), .Carry(halfadder_6_carry));
  HalfAdder halfadder_7 (.input_X(X6), .input_Y(Y6), .Sum(halfadder_7_sum), .Carry(halfadder_7_carry));
  HalfAdder halfadder_8 (.input_X(X7), .input_Y(Y7), .Sum(halfadder_8_sum), .Carry(halfadder_8_carry));
  HalfAdder halfadder_9 (.input_X(halfadder_1_sum), .input_Y(Cin), .Sum(S0), .Carry(halfadder_9_carry));
  HalfAdder halfadder_10 (.input_X(halfadder_2_sum), .input_Y(or_1_out), .Sum(S1), .Carry(halfadder_10_carry));
  HalfAdder halfadder_11 (.input_X(halfadder_3_sum), .input_Y(or_2_out), .Sum(S2), .Carry(halfadder_11_carry));
  HalfAdder halfadder_12 (.input_X(halfadder_4_sum), .input_Y(or_3_out), .Sum(S3), .Carry(halfadder_12_carry));
  HalfAdder halfadder_13 (.input_X(halfadder_5_sum), .input_Y(or_4_out), .Sum(S4), .Carry(halfadder_13_carry));
  HalfAdder halfadder_14 (.input_X(halfadder_6_sum), .input_Y(or_5_out), .Sum(S5), .Carry(halfadder_14_carry));
  HalfAdder halfadder_15 (.input_X(halfadder_7_sum), .input_Y(or_6_out), .Sum(S6), .Carry(halfadder_15_carry));
  HalfAdder halfadder_16 (.input_X(halfadder_8_sum), .input_Y(or_7_out), .Sum(S7), .Carry(halfadder_16_carry));
  or or_1 (or_1_out, halfadder_9_carry, halfadder_1_carry);
  or or_2 (or_2_out, halfadder_10_carry, halfadder_2_carry);
  or or_3 (or_3_out, halfadder_11_carry, halfadder_3_carry);
  or or_4 (or_4_out, halfadder_12_carry, halfadder_4_carry);
  or or_5 (or_5_out, halfadder_13_carry, halfadder_5_carry);
  or or_6 (or_6_out, halfadder_14_carry, halfadder_6_carry);
  or or_7 (or_7_out, halfadder_15_carry, halfadder_7_carry);
  or or_8 (or_8_out, halfadder_16_carry, halfadder_8_carry);
endmodule

module Decoder (
  input  [1:0] in_1,
  output O0,
  output O1,
  output O2,
  output O3
);

  wire not_1_out, not_2_out;

  not not_1 (not_1_out, in_1[0]);
  not not_2 (not_2_out, in_1[1]);
  and u_O0 (O0, not_1_out, not_2_out);
  and u_O1 (O1, in_1[0], not_2_out);
  and u_O2 (O2, not_1_out, in_1[1]);
  and u_O3 (O3, in_1[0], in_1[1]);
endmodule

module Decoder_YouTube (
  input  A,
  input  B,
  input  Cin,
  output S,
  output C0
);

  wire not_1_out, not_2_out, not_3_out, O1_out, O2_out, O3_out, O4_out, O5_out, O6_2_out, O6_out;

  not not_1 (not_1_out, A);
  not not_2 (not_2_out, B);
  not not_3 (not_3_out, Cin);
  // AND_Gate O0 has open pins: in0=not_1_out, in1=not_2_out, in2=not_3_out, out=open
  and O1 (O1_out, not_1_out, not_2_out, Cin);
  and O2 (O2_out, not_1_out, B, not_3_out);
  and O3 (O3_out, not_1_out, B, Cin);
  and O4 (O4_out, A, not_2_out, not_3_out);
  and O5 (O5_out, A, not_2_out, Cin);
  and O6 (O6_out, A, B, not_3_out);
  and O6_2 (O6_2_out, A, B, Cin);
  or or_1 (S, O1_out, O2_out, O4_out, O6_2_out);
  or or_2 (C0, O3_out, O5_out, O6_out, O6_2_out);
endmodule

module Adder_4bit_UsingDecoder (
  input  Cin,
  input  X0,
  input  Y0,
  input  X1,
  input  Y1,
  input  X3,
  input  Y3,
  input  X4,
  input  Y4,
  output S0,
  output S1,
  output S2,
  output S3
);

  wire decoder_youtube_1_c0, decoder_youtube_2_c0, decoder_youtube_3_c0, decoder_youtube_4_c0;

  Decoder_YouTube decoder_youtube_1 (.A(Cin), .B(X0), .Cin(Y0), .S(S0), .C0(decoder_youtube_1_c0));
  Decoder_YouTube decoder_youtube_2 (.A(decoder_youtube_1_c0), .B(X1), .Cin(Y1), .S(S1), .C0(decoder_youtube_2_c0));
  Decoder_YouTube decoder_youtube_3 (.A(decoder_youtube_2_c0), .B(X3), .Cin(Y3), .S(S2), .C0(decoder_youtube_3_c0));
  Decoder_YouTube decoder_youtube_4 (.A(decoder_youtube_3_c0), .B(X4), .Cin(Y4), .S(S3), .C0(decoder_youtube_4_c0));
endmodule

module Multiplexer (
  input  [7:0] in_1,
  input  [7:0] in_2,
  input  [7:0] in_3,
  input  [7:0] in_4,
  input  [1:0] in_5,
  input  [7:0] in_6,
  input  [7:0] in_7,
  input  [7:0] in_8,
  input  [7:0] in_9,
  input  [1:0] in_10,
  output [7:0] out_11,
  output [7:0] out_12
);

  wire [7:0] multiplexer_1_out, multiplexer_2_out;

  Multiplexer_part #(.width(8), .enable("false")) multiplexer_1 (
    .in0(in_1), .in1(in_2), .out(multiplexer_1_out), .sel(in_5[0]));
  Multiplexer_part #(.width(8), .enable("false")) multiplexer_2 (
    .in0(in_3), .in1(in_4), .out(multiplexer_2_out), .sel(in_5[0]));
  Multiplexer_part #(.width(8), .enable("false")) multiplexer_3 (
    .in0(multiplexer_1_out), .in1(multiplexer_2_out), .out(out_11), .sel(in_5[1]));
  Multiplexer_part #(.select(2), .width(8), .enable("false")) multiplexer_4 (
    .in0(in_6), .in1(in_7), .in2(in_8), .in3(in_9), .out(out_12), .sel(in_10));
endmodule

module Multiplexer2 (
  input  [7:0] in_1,
  input  [7:0] in_2,
  input  [7:0] in_3,
  input  [7:0] in_4,
  input  [7:0] in_5,
  input  [7:0] in_6,
  input  [7:0] in_7,
  input  [7:0] in_8,
  input  [7:0] in_9,
  input  [7:0] in_10,
  input  [7:0] in_11,
  input  [7:0] in_12,
  input  [7:0] in_13,
  input  [7:0] in_14,
  input  [7:0] in_15,
  input  [7:0] in_16,
  input  [3:0] in_17,
  output [7:0] out_18
);

  wire [7:0] multiplexer_1_out, multiplexer_2_out, multiplexer_3_out, multiplexer_4_out;

  Multiplexer_part #(.select(2), .width(8), .enable("false")) multiplexer_1 (
    .in0(in_1), .in1(in_2), .in2(in_3), .in3(in_4), .out(multiplexer_1_out), .sel(in_17[1:0]));
  Multiplexer_part #(.select(2), .width(8), .enable("false")) multiplexer_2 (
    .in0(in_5), .in1(in_6), .in2(in_7), .in3(in_8), .out(multiplexer_2_out), .sel(in_17[1:0]));
  Multiplexer_part #(.select(2), .width(8), .enable("false")) multiplexer_3 (
    .in0(in_9), .in1(in_10), .in2(in_11), .in3(in_12), .out(multiplexer_3_out), .sel(in_17[1:0]));
  Multiplexer_part #(.select(2), .width(8), .enable("false")) multiplexer_4 (
    .in0(in_13), .in1(in_14), .in2(in_15), .in3(in_16), .out(multiplexer_4_out), .sel(in_17[1:0]));
  Multiplexer_part #(.select(2), .width(8), .enable("false")) multiplexer_5 (
    .in0(multiplexer_1_out), .in1(multiplexer_2_out), .in2(multiplexer_3_out), .in3(multiplexer_4_out),
    .out(out_18), .sel(in_17[3:2]));
endmodule
