// Logisim project Assignment.circ as structural Verilog: 7 circuits, main circuit main
module main (
  output out_1,
  output out_2
);

  wire blackbox_1_q0new, blackbox_1_q1new, clock_1_out;

  Clock clock_1 (.out(clock_1_out));
  BlackBox blackbox_1 (.Q0(out_1), .Q1(out_2), .C(clock_1_out), .Q0new(blackbox_1_q0new), .Q1new(blackbox_1_q1new));
  main3 main3_1 ();  // open: out_1, out_2, out_3
  D_Flip_Flop Q0 (.D(blackbox_1_q0new), .clk(clock_1_out), .Q(out_1));  // open: Qn, preset, reset
  D_Flip_Flop Q1 (.D(blackbox_1_q1new), .clk(clock_1_out), .Q(out_2));  // open: Qn, preset, reset
endmodule

module BlackBox (
  input  Q0,
  input  Q1,
  input  C,
  output Q0new,
  output Q1new
);

  wire and_1_out, and_2_out, and_3_out, and_4_out, and_5_out, not_1_out, not_2_out, not_3_out, not_4_out;

  not not_1 (not_1_out, Q0);
  not not_2 (not_2_out, C);
  not not_3 (not_3_out, Q1);
  not not_4 (not_4_out, not_2_out);
  and and_1 (and_1_out, Q0, not_4_out);
  and and_2 (and_2_out, not_1_out, not_2_out);
  and and_3 (and_3_out, Q0, not_3_out);
  and and_4 (and_4_out, Q0, not_4_out);
  and and_5 (and_5_out, not_1_out, Q1, not_2_out);
  or or_1 (Q0new, and_1_out, and_2_out);
  or or_2 (Q1new, and_3_out, and_4_out, and_5_out);
endmodule

module main2 (
  output out_1,
  output out_2
);

  wire BlackBox_q0new, BlackBox_q1new, clock_1_out;

  Clock clock_1 (.out(clock_1_out));
  BlackBox2 BlackBox (.Q1(out_1), .Q0(out_2), .C(clock_1_out), .Q0new(BlackBox_q0new), .Q1new(BlackBox_q1new));
  D_Flip_Flop Q0 (.D(BlackBox_q0new), .clk(clock_1_out), .Q(out_1));  // open: Qn, preset, reset
  D_Flip_Flop Q1 (.D(BlackBox_q1new), .clk(clock_1_out), .Q(out_2));  // open: Qn, preset, reset
endmodule

module BlackBox2 (
  input  Q1,
  input  Q0,
  input  C,
  output Q0new,
  output Q1new
);

  wire and_1_out, and_2_out, and_3_out, and_4_out, and_5_out, not_1_out, not_2_out, not_3_out, not_4_out;

  not not_1 (not_1_out, C);
  not not_2 (not_2_out, Q0);
  not not_3 (not_3_out, Q1);
  not not_4 (not_4_out, not_1_out);
  and and_1 (and_1_out, not_2_out, Q1);
  and and_2 (and_2_out, Q1, not_4_out);
  and and_3 (and_3_out, Q0, not_3_out, not_1_out);
  and and_4 (and_4_out, not_2_out, not_1_out);
  and and_5 (and_5_out, Q0, not_4_out);
  or or_1 (Q0new, and_1_out, and_2_out, and_3_out);
  or or_2 (Q1new, and_4_out, and_5_out);
endmodule

module ROM (
  input  Q0,
  input  Q1,
  input  C,
  output Q0new,
  output Q1new
);

  wire [2:2] not_1_out;

  not not_1 (not_1_out[2], C);
  ROM_part #(.addrWidth(3), .dataWidth(2)) rom_1 (.addr({not_1_out[2], Q1, Q0}), .data({Q1new, Q0new}));

  // Notes on the sheet:
  //   contents of rom_1 (hex, n*v repeats v):
  //   1 2 3 0 1 2 3
endmodule

module main3 (
  output out_1,
  output out_2,
  output out_3
);

  wire clock_1_out;
  wire [2:0] rom_1_data;
  wire [3:3] not_1_out;

  Clock clock_1 (.out(clock_1_out));
  ROM_part #(.addrWidth(4), .dataWidth(3)) rom_1 (.addr({not_1_out[3], out_1, out_2, out_3}), .data(rom_1_data));
  not not_1 (not_1_out[3], clock_1_out);
  D_Flip_Flop d_ff_1 (.D(rom_1_data[2]), .clk(clock_1_out), .Q(out_1));  // open: Qn, preset, reset
  D_Flip_Flop d_ff_2 (.D(rom_1_data[1]), .clk(clock_1_out), .Q(out_2));  // open: Qn, preset, reset
  D_Flip_Flop d_ff_3 (.D(rom_1_data[0]), .clk(clock_1_out), .Q(out_3));  // open: Qn, preset, reset

  // Notes on the sheet:
  //   contents of rom_1 (hex, n*v repeats v):
  //   0 0 1 1 2 2 3 3 4 4 5 5 6 6
endmodule

module ROM2 (
  input  Q0,
  input  Q1,
  input  Q2,
  input  C,
  output Q0new,
  output Q1new,
  output Q2new
);

  wire [3:3] not_1_out;

  not not_1 (not_1_out[3], C);
  ROM_part #(.addrWidth(4), .dataWidth(3)) rom_1 (.addr({not_1_out[3], Q2, Q1, Q0}), .data({Q2new, Q1new, Q0new}));

  // Notes on the sheet:
  //   contents of rom_1 (hex, n*v repeats v):
  //   0 0 1 1 2 2 3 3 4 4 5 5 6 6
endmodule
